// Logisim project ALU.circ as structural Verilog
module main (
  input  [31:0] A,
  input  [31:0] B,
  input  [3:0] Op,
  input  [4:0] Sa,
  output [31:0] C,
  output V
);

  wire and_1_out, and_2_out, and_3_out, and_4_out, and_5_out, and_6_out, and_7_out, bitselector_1_out,
       nand_1_out, not_1_out, not_2_out, not_3_out, not_4_out, not_5_out;
  wire [31:0] lrshift32_1_c;

  not not_1 (not_1_out, Op[1]);
  not not_2 (not_2_out, Op[3]);
  not not_3 (not_3_out, Op[3]);
  BitSelector #(.width(32)) bitselector_1 (.in(B), .out(bitselector_1_out), .sel({5{1'b1}}));
  and and_1 (and_1_out, not_3_out, Op[1]);
  and and_2 (and_2_out, not_1_out, not_2_out);
  not not_4 (not_4_out, Op[2]);
  and and_3 (and_3_out, Op[0], Op[3]);
  AddSub32 addsub32_1 (.A(A), .Opcode(Op[2]), .B(B));  // open: V, Out
  nand nand_1 (nand_1_out, not_4_out, and_2_out);
  not not_5 (not_5_out, Op[0]);
  and and_4 (and_4_out, nand_1_out, Op[0]);
  and and_5 (and_5_out, not_5_out, Op[3]);
  and and_6 (and_6_out, bitselector_1_out, and_4_out);
  LRShift32 lrshift32_1 (.Op(Op[2]), .B(B), .Sa(Sa), .Cin(and_7_out), .C(lrshift32_1_c));
  and and_7 (and_7_out, and_6_out, nand_1_out);
  Logic32 logic32_1 (.A(A), .B(B), .Op(Op[2:1]), .O(C));

  // Notes on the sheet:
  //   Add/Subtract
  //   compare
  //   Shifting
  //   Logic
endmodule

module LeftShift32 (
  input  Cn,
  input  [31:0] B,
  input  [4:0] Sa,
  output [31:0] C
);

  wire [31:0] multiplexer_1_out, multiplexer_2_out, multiplexer_3_out;
  wire [31:16] multiplexer_4_out, multiplexer_4_out_2;

  Multiplexer #(.width(32), .enable("false")) multiplexer_1 (
    .in0(B), .in1({B[30:0], Cn}), .out(multiplexer_1_out), .sel(Sa[0]));
  Multiplexer #(.width(32), .enable("false")) multiplexer_2 (
    .in0(multiplexer_1_out), .in1({multiplexer_1_out[29:0], {2{Cn}}}), .out(multiplexer_2_out), .sel(Sa[1]));
  Multiplexer #(.width(32), .enable("false")) multiplexer_3 (
    .in0(multiplexer_2_out), .in1({multiplexer_2_out[27:0], {4{Cn}}}), .out(multiplexer_3_out), .sel(Sa[2]));
  Multiplexer #(.width(32), .enable("false")) multiplexer_4 (
    .in0(multiplexer_3_out), .in1({multiplexer_3_out[23:0], {8{Cn}}}),
    .out({multiplexer_4_out_2, multiplexer_4_out}), .sel(Sa[3]));
  Multiplexer #(.width(32), .enable("false")) multiplexer_5 (
    .in0({multiplexer_4_out_2, multiplexer_4_out}), .in1({multiplexer_4_out, {16{Cn}}}), .out(C), .sel(Sa[4]));
endmodule

module LRShift32 (
  input  Op,
  input  [31:0] B,
  input  [4:0] Sa,
  input  Cin,
  output [31:0] C
);

  wire [31:0] flip32_1_flipa, flip32_2_flipa, leftshift32_1_c, multiplexer_1_out;

  Flip32 flip32_1 (.A(B), .FlipA(flip32_1_flipa));
  Multiplexer #(.width(32), .enable("false")) multiplexer_1 (
    .in0(B), .in1(flip32_1_flipa), .out(multiplexer_1_out), .sel(Op));
  LeftShift32 leftshift32_1 (.Cn(Cin), .B(multiplexer_1_out), .Sa(Sa), .C(leftshift32_1_c));
  Flip32 flip32_2 (.A(leftshift32_1_c), .FlipA(flip32_2_flipa));
  Multiplexer #(.width(32), .enable("false")) multiplexer_2 (
    .in0(leftshift32_1_c), .in1(flip32_2_flipa), .out(C), .sel(Op));
endmodule

module Flip32 (
  input  [31:0] A,
  output [31:0] FlipA
);


  assign FlipA = {A[0], A[1], A[2], A[3], A[4], A[5], A[6], A[7], A[8], A[9], A[10], A[11], A[12], A[13], A[14], A[15], A[16], A[17], A[18], A[19], A[20], A[21], A[22], A[23], A[24], A[25], A[26], A[27], A[28], A[29], A[30], A[31]};
endmodule

module Add1 (
  input  A,
  input  B,
  input  C_in,
  output S,
  output C_out
);

  wire and_1_out, and_2_out, xor_1_out;

  xor xor_1 (xor_1_out, A, B);
  xor xor_2 (S, xor_1_out, C_in);
  and and_1 (and_1_out, xor_1_out, C_in);
  and and_2 (and_2_out, B, A);
  xor xor_3 (C_out, and_1_out, and_2_out);
endmodule

module Add4 (
  input  [3:0] A_4,
  input  [3:0] A_4_2,
  input  C_in,
  output C_out,
  output [3:0] Out
);

  wire add1_1_c_out, add1_2_c_out, add1_3_c_out;

  Add1 add1_1 (.A(A_4[0]), .B(A_4_2[0]), .C_in(C_in), .S(Out[0]), .C_out(add1_1_c_out));
  Add1 add1_2 (.A(A_4[1]), .B(A_4_2[1]), .C_in(add1_1_c_out), .S(Out[1]), .C_out(add1_2_c_out));
  Add1 add1_3 (.A(A_4[2]), .B(A_4_2[2]), .C_in(add1_2_c_out), .S(Out[2]), .C_out(add1_3_c_out));
  Add1 add1_4 (.A(A_4[3]), .B(A_4_2[3]), .C_in(add1_3_c_out), .S(Out[3]), .C_out(C_out));
endmodule

module Add8 (
  input  [7:0] A_8,
  input  [7:0] B_8,
  input  C_in,
  output C_out,
  output [7:0] Out
);

  wire add4_1_c_out;

  Add4 add4_1 (.A_4(A_8[3:0]), .A_4_2(B_8[3:0]), .C_in(C_in), .C_out(add4_1_c_out), .Out(Out[3:0]));
  Add4 add4_2 (.A_4(A_8[7:4]), .A_4_2(B_8[7:4]), .C_in(add4_1_c_out), .C_out(C_out), .Out(Out[7:4]));
endmodule

module Add16 (
  input  [15:0] B_8,
  input  [15:0] A_8,
  input  C_in,
  output C_out,
  output [15:0] Out
);

  wire add8_1_c_out;

  Add8 add8_1 (.A_8(A_8[7:0]), .B_8(B_8[7:0]), .C_in(C_in), .Out(Out[7:0]), .C_out(add8_1_c_out));
  Add8 add8_2 (.A_8(B_8[15:8]), .B_8(A_8[15:8]), .C_in(add8_1_c_out), .Out(Out[15:8]), .C_out(C_out));
endmodule

module StdAdd32 (
  input  [31:0] B_8,
  input  [31:0] A_8,
  input  C_in,
  output C_out,
  output [31:0] Out
);

  wire add16_1_c_out;

  Add16 add16_1 (.B_8(B_8[15:0]), .A_8(A_8[15:0]), .C_in(C_in), .Out(Out[15:0]), .C_out(add16_1_c_out));
  Add16 add16_2 (.B_8(B_8[31:16]), .A_8(A_8[31:16]), .C_in(add16_1_c_out), .Out(Out[31:16]), .C_out(C_out));
endmodule

module Sub32 (
  input  [31:0] A,
  input  [31:0] B,
  output [31:0] Out
);

  wire [31:0] not_1_out;

  assign not_1_out = ~B;  // NOT_Gate not_1, 32 bits wide
  StdAdd32 stdadd32_1 (.B_8(A), .A_8(not_1_out), .C_in(1'b1), .Out(Out));  // open: C_out
endmodule

module AddSub32 (
  input  [31:0] A,
  input  Opcode,
  input  [31:0] B,
  output V,
  output [31:0] Out
);

  wire [31:0] multiplexer_1_out, not_1_out;

  assign not_1_out = ~B;  // NOT_Gate not_1, 32 bits wide
  Multiplexer #(.width(32), .enable("false")) multiplexer_1 (
    .in0(B), .in1(not_1_out), .out(multiplexer_1_out), .sel(Opcode));
  StdAdd32 stdadd32_1 (.B_8(A), .A_8(multiplexer_1_out), .C_in(Opcode), .Out(Out), .C_out(V));
endmodule

module Logic32 (
  input  [31:0] A,
  input  [31:0] B,
  input  [1:0] Op,
  output [31:0] O
);

  wire [31:0] and_1_out, nor_1_out, or_1_out, xor_1_out;

  assign and_1_out = A & B;  // AND_Gate and_1, 32 bits wide
  assign or_1_out = A | B;  // OR_Gate or_1, 32 bits wide
  assign nor_1_out = ~(A | B);  // NOR_Gate nor_1, 32 bits wide
  assign xor_1_out = A ^ B;  // XOR_Gate xor_1, 32 bits wide
  Multiplexer #(.select(2), .width(32), .enable("false")) multiplexer_1 (
    .in0(and_1_out), .in1(or_1_out), .in2(xor_1_out), .in3(nor_1_out), .out(O), .sel(Op));

  // Notes on the sheet:
  //   middle two bits
endmodule

module blah (
  input  a,
  input  b,
  input  l,
  input  r,
  output res
);

  wire and_1_out, and_2_out, and_3_out, and_4_out, and_5_out, and_6_out, not_1_out, not_2_out, not_3_out,
       not_4_out, not_5_out, not_6_out, not_7_out, not_8_out, not_9_out;

  not not_1 (not_1_out, a);
  not not_2 (not_2_out, b);
  not not_3 (not_3_out, l);
  not not_4 (not_4_out, a);
  not not_5 (not_5_out, r);
  not not_6 (not_6_out, l);
  not not_7 (not_7_out, b);
  not not_8 (not_8_out, r);
  not not_9 (not_9_out, l);
  and and_1 (and_1_out, not_1_out, not_2_out, l, r);
  and and_2 (and_2_out, b, not_3_out, r);
  and and_3 (and_3_out, not_4_out, b, l, not_5_out);
  and and_4 (and_4_out, a, not_6_out, r);
  and and_5 (and_5_out, a, not_7_out, l, not_8_out);
  and and_6 (and_6_out, a, b, not_9_out);
  or or_1 (res, and_1_out, and_2_out, and_3_out, and_4_out, and_5_out, and_6_out);
endmodule

module Compare32 (
  input  [31:0] A,
  input  [31:0] B,
  input  [1:0] Op,
  output [31:0] out_4
);

  AddSub32 addsub32_1 (.A(A), .Opcode(1'b1), .B(B), .Out(out_4));  // open: V
  // NAND_Gate nand_1 has open pins: in0=out_4[0], in1=out_4[1], in2=out_4[2], in3=out_4[3], in4=out_4[4], in5=out_4[5], in6=out_4[6], in7=out_4[7], in8=out_4[8], in9=out_4[9], in10=out_4[10], in11=out_4[11], in12=out_4[12], in13=out_4[13], in14=out_4[14], in15=out_4[15], in16=out_4[16], in17=out_4[17], in18=out_4[18], in19=out_4[19], in20=out_4[20], in21=out_4[21], in22=out_4[22], in23=out_4[23], in24=out_4[24], in25=out_4[25], in26=out_4[26], in27=out_4[27], in28=out_4[28], in29=out_4[29], in30=out_4[30], in31=out_4[31], out=open

  // Notes on the sheet:
  //   2 middle bits
endmodule
