// Logisim project Processor.circ as structural Verilog: 4 circuits, main circuit main
module main (
);

  Register_File register_file_1 ();  // open: D, Rw, W, Ra, Rb, Qa, Qb
endmodule

// rising
module Register_File (
  input  [31:0] D,
  input  [4:0] Rw,
  input  W,
  input  [4:0] Ra,
  input  [4:0] Rb,
  output [31:0] Qa,
  output [31:0] Qb
);

  wire and_1_out, and_2_out, and_3_out, and_4_out, and_5_out, and_6_out, and_7_out, and_8_out, and_9_out,
       and_10_out, and_11_out, and_12_out, and_13_out, and_14_out, and_15_out, and_16_out, and_17_out,
       and_18_out, and_19_out, and_20_out, and_21_out, and_22_out, and_23_out, and_24_out, and_25_out,
       and_26_out, and_27_out, and_28_out, and_29_out, and_30_out, and_31_out, clock_1_out, decoder_1_out1,
       decoder_1_out2, decoder_1_out3, decoder_1_out4, decoder_1_out5, decoder_1_out6, decoder_1_out7,
       decoder_1_out8, decoder_1_out9, decoder_1_out10, decoder_1_out11, decoder_1_out12, decoder_1_out13,
       decoder_1_out14, decoder_1_out15, decoder_1_out16, decoder_1_out17, decoder_1_out18, decoder_1_out19,
       decoder_1_out20, decoder_1_out21, decoder_1_out22, decoder_1_out23, decoder_1_out25, decoder_1_out26,
       decoder_1_out27, decoder_1_out28, decoder_1_out29, decoder_1_out30, decoder_1_out31;
  wire [31:0] _0_q, _1_q, _2_q, _3_q, _4_q, _5_q, _6_q, _7_q, _8_q, _9_q, _10_q, _11_q, _12_q, _13_q, _14_q,
       _15_q, _16_q, _17_q, _18_q, _19_q, _20_q, _21_q, _22_q, _23_q, _24_q, _25_q, _26_q, _27_q, _28_q,
       _29_q, _31_2_q, _31_q;

  Decoder #(.select(5), .enable("false")) decoder_1 (
    .out1(decoder_1_out1), .out2(decoder_1_out2), .out3(decoder_1_out3), .out4(decoder_1_out4),
    .out5(decoder_1_out5), .out6(decoder_1_out6), .out7(decoder_1_out7), .out8(decoder_1_out8),
    .out9(decoder_1_out9), .out10(decoder_1_out10), .out11(decoder_1_out11), .out12(decoder_1_out12),
    .out13(decoder_1_out13), .out14(decoder_1_out14), .out15(decoder_1_out15), .out16(decoder_1_out16),
    .out17(decoder_1_out17), .out18(decoder_1_out18), .out19(decoder_1_out19), .out20(decoder_1_out20),
    .out21(decoder_1_out21), .out22(decoder_1_out22), .out23(decoder_1_out23), .out24(W),
    .out25(decoder_1_out25), .out26(decoder_1_out26), .out27(decoder_1_out27), .out28(decoder_1_out28),
    .out29(decoder_1_out29), .out30(decoder_1_out30), .out31(decoder_1_out31), .sel(Rw));  // open: out0
  Clock clock_1 (.out(clock_1_out));
  and and_1 (and_1_out, W, decoder_1_out1);
  and and_2 (and_2_out, W, decoder_1_out2);
  and and_3 (and_3_out, W, decoder_1_out3);
  and and_4 (and_4_out, W, decoder_1_out4);
  and and_5 (and_5_out, W, decoder_1_out5);
  and and_6 (and_6_out, W, decoder_1_out6);
  and and_7 (and_7_out, W, decoder_1_out7);
  Register #(.width(32)) _0 (.Q(_0_q));  // open: D, en, clk, clr
  Register #(.width(32)) _1 (.D(D), .en(and_1_out), .Q(_1_q), .clk(clock_1_out));  // open: clr
  Register #(.width(32)) _2 (.D(D), .en(and_2_out), .Q(_2_q), .clk(clock_1_out));  // open: clr
  Register #(.width(32)) _3 (.D(D), .en(and_3_out), .Q(_3_q), .clk(clock_1_out));  // open: clr
  Register #(.width(32)) _4 (.D(D), .en(and_4_out), .Q(_4_q), .clk(clock_1_out));  // open: clr
  Register #(.width(32)) _5 (.D(D), .en(and_5_out), .Q(_5_q), .clk(clock_1_out));  // open: clr
  Register #(.width(32)) _6 (.D(D), .en(and_6_out), .Q(_6_q), .clk(clock_1_out));  // open: clr
  Register #(.width(32)) _7 (.D(D), .en(and_7_out), .Q(_7_q), .clk(clock_1_out));  // open: clr
  and and_8 (and_8_out, W, decoder_1_out8);
  and and_9 (and_9_out, W, decoder_1_out9);
  and and_10 (and_10_out, W, decoder_1_out10);
  and and_11 (and_11_out, W, decoder_1_out11);
  and and_12 (and_12_out, W, decoder_1_out12);
  and and_13 (and_13_out, W, decoder_1_out13);
  and and_14 (and_14_out, W, decoder_1_out14);
  and and_15 (and_15_out, W, decoder_1_out15);
  Register #(.width(32)) _8 (.D(D), .en(and_8_out), .Q(_8_q), .clk(clock_1_out));  // open: clr
  Register #(.width(32)) _9 (.D(D), .en(and_9_out), .Q(_9_q), .clk(clock_1_out));  // open: clr
  Register #(.width(32)) _10 (.D(D), .en(and_10_out), .Q(_10_q), .clk(clock_1_out));  // open: clr
  Register #(.width(32)) _11 (.D(D), .en(and_11_out), .Q(_11_q), .clk(clock_1_out));  // open: clr
  Register #(.width(32)) _12 (.D(D), .en(and_12_out), .Q(_12_q), .clk(clock_1_out));  // open: clr
  Register #(.width(32)) _13 (.D(D), .en(and_13_out), .Q(_13_q), .clk(clock_1_out));  // open: clr
  Register #(.width(32)) _14 (.D(D), .en(and_14_out), .Q(_14_q), .clk(clock_1_out));  // open: clr
  Register #(.width(32)) _15 (.D(D), .en(and_15_out), .Q(_15_q), .clk(clock_1_out));  // open: clr
  and and_16 (and_16_out, W, decoder_1_out16);
  and and_17 (and_17_out, W, decoder_1_out17);
  and and_18 (and_18_out, W, decoder_1_out18);
  and and_19 (and_19_out, W, decoder_1_out19);
  and and_20 (and_20_out, W, decoder_1_out20);
  and and_21 (and_21_out, W, decoder_1_out21);
  and and_22 (and_22_out, W, decoder_1_out22);
  and and_23 (and_23_out, W, decoder_1_out23);
  Register #(.width(32)) _16 (.D(D), .en(and_16_out), .Q(_16_q), .clk(clock_1_out));  // open: clr
  Register #(.width(32)) _17 (.D(D), .en(and_17_out), .Q(_17_q), .clk(clock_1_out));  // open: clr
  Register #(.width(32)) _18 (.D(D), .en(and_18_out), .Q(_18_q), .clk(clock_1_out));  // open: clr
  Register #(.width(32)) _19 (.D(D), .en(and_19_out), .Q(_19_q), .clk(clock_1_out));  // open: clr
  Register #(.width(32)) _20 (.D(D), .en(and_20_out), .Q(_20_q), .clk(clock_1_out));  // open: clr
  Register #(.width(32)) _21 (.D(D), .en(and_21_out), .Q(_21_q), .clk(clock_1_out));  // open: clr
  Register #(.width(32)) _22 (.D(D), .en(and_22_out), .Q(_22_q), .clk(clock_1_out));  // open: clr
  Register #(.width(32)) _23 (.D(D), .en(and_23_out), .Q(_23_q), .clk(clock_1_out));  // open: clr
  and and_24 (and_24_out, W, W);
  and and_25 (and_25_out, W, decoder_1_out25);
  and and_26 (and_26_out, W, decoder_1_out26);
  and and_27 (and_27_out, W, decoder_1_out27);
  and and_28 (and_28_out, W, decoder_1_out28);
  and and_29 (and_29_out, W, decoder_1_out29);
  and and_30 (and_30_out, W, decoder_1_out30);
  and and_31 (and_31_out, W, decoder_1_out31);
  Register #(.width(32)) _24 (.D(D), .en(and_24_out), .Q(_24_q), .clk(clock_1_out));  // open: clr
  Register #(.width(32)) _25 (.D(D), .en(and_25_out), .Q(_25_q), .clk(clock_1_out));  // open: clr
  Register #(.width(32)) _26 (.D(D), .en(and_26_out), .Q(_26_q), .clk(clock_1_out));  // open: clr
  Register #(.width(32)) _27 (.D(D), .en(and_27_out), .Q(_27_q), .clk(clock_1_out));  // open: clr
  Register #(.width(32)) _28 (.D(D), .en(and_28_out), .Q(_28_q), .clk(clock_1_out));  // open: clr
  Register #(.width(32)) _29 (.D(D), .en(and_29_out), .Q(_29_q), .clk(clock_1_out));  // open: clr
  Register #(.width(32)) _31 (.D(D), .en(and_30_out), .Q(_31_q), .clk(clock_1_out));  // open: clr
  Register #(.width(32)) _31_2 (.D(D), .en(and_31_out), .Q(_31_2_q), .clk(clock_1_out));  // open: clr
  Multiplexer #(.select(5), .width(32), .enable("false")) multiplexer_1 (
    .in0(_0_q), .in1(_1_q), .in2(_2_q), .in3(_3_q), .in4(_4_q), .in5(_5_q), .in6(_6_q), .in7(_7_q),
    .in8(_8_q), .in9(_9_q), .in10(_10_q), .in11(_11_q), .in12(_12_q), .in13(_13_q), .in14(_14_q),
    .in15(_15_q), .in16(_16_q), .in17(_17_q), .in18(_18_q), .in19(_19_q), .in20(_20_q), .in21(_21_q),
    .in22(_22_q), .in23(_23_q), .in24(_24_q), .in25(_25_q), .in26(_26_q), .in27(_27_q), .in28(_28_q),
    .in29(_29_q), .in30(_31_q), .in31(_31_2_q), .out(Qa), .sel(Ra));
  Multiplexer #(.select(5), .width(32), .enable("false")) multiplexer_2 (
    .in0(_0_q), .in1(_1_q), .in2(_2_q), .in3(_3_q), .in4(_4_q), .in5(_5_q), .in6(_6_q), .in7(_7_q),
    .in8(_8_q), .in9(_9_q), .in10(_10_q), .in11(_11_q), .in12(_12_q), .in13(_13_q), .in14(_14_q),
    .in15(_15_q), .in16(_16_q), .in17(_17_q), .in18(_18_q), .in19(_19_q), .in20(_20_q), .in21(_21_q),
    .in22(_22_q), .in23(_23_q), .in24(_24_q), .in25(_25_q), .in26(_26_q), .in27(_27_q), .in28(_28_q),
    .in29(_29_q), .in30(_31_q), .in31(_31_2_q), .out(Qb), .sel(Rb));
endmodule

module Fetch (
  input  in_1,
  input  in_2,
  input  in_3,
  input  in_4
);

  wire [7:0] n8_bit_1_p2, n8_bit_1_p4;

  ROM #(.dataWidth(32)) rom_1 (.addr(n8_bit_1_p2));  // open: data, sel
  // _8_bit 8_bit_1: pin names not known; wires that end beside it: 1'b0, n8_bit_1_p2, 8'h4, n8_bit_1_p4
  Counter counter_1 (
    .load(in_4), .D(n8_bit_1_p4), .count(in_3), .Q(n8_bit_1_p2), .clk(in_1), .clr(in_2));  // open: carry
endmodule

module _4Count (
  input  [7:0] currLoc,
  input  in_2,
  input  in_3,
  input  in_4,
  input  in_5
);

  wire [7:0] n8_bit_1_p4, n8_bit_1_p5;

  // _8_bit 8_bit_1: pin names not known; wires that end beside it: 1'b0, currLoc, 8'h4, n8_bit_1_p4, n8_bit_1_p5
  Counter counter_1 (
    .load(in_5), .D(n8_bit_1_p4), .count(in_4), .Q(n8_bit_1_p5), .clk(in_2), .clr(in_3));  // open: carry

  // Notes on the sheet:
  //   TODO: have a clock to increment the counter by the new one
endmodule
