// Logisim project execute.circ as structural Verilog: 1 circuit, main circuit main
module main (
  input  [31:0] A,
  input  [31:0] B,
  input  [31:0] Imm
);

  Multiplexer #(.width(32), .enable("false")) multiplexer_1 (.in0(B), .in1(Imm));  // open: out, sel
endmodule
